# Fritzing sketch OWGeneric_SensorStation (saved by Fritzing 0.8.5b)
breadboards: 4

parts:
  U2 = MAGJACK-POE [package=magjack-poe]
  U3 = GAS_SENSOR [package=mq-3]
  U4 = GAS_SENSOR [package=mq-3]
  U5 = GAS_SENSOR [package=mq-3]
  U6 = GAS_SENSOR [package=mq-3]
  U7 = GAS_SENSOR [package=mq-3]
  U8 = GAS_SENSOR [package=mq-3]
  Bauteil4 = Breakout Board for Electret Microphone
  LED1 = Super Flux RGB LED (com. cathode)
  Bauteil5 = Arduino Nano (Rev3.0)
  U9 = 74HC4067 [package=ssop24]
  Bauteil6 = Ambient Light Sensor (TEMT6000 Breakout Board)
  Bauteil7 = Color Sensor Breakout ADJD-S311  # not connected
  Bauteil8 = 9 Degrees of Freedom - Sensor Stick  # not connected
  U10 = Barometric Pressure Sensor  # not connected
  JP4 = Header 6 [package=molex-1x6_lock]
  R3 = Resistor [tolerance=±5% resistance=150 package=THT]
  C3 = Capacitor Polarized [part_number=220uF package=cpol-radial-10uf-25v]

nets:
  GND: U2.RD+, U2.SHIELD, U3.H1, U4.H1, U5.H1, U6.H1, U7.H1, U8.H1, Bauteil5.GND, U9.GND, U9.EN, JP4.2, JP4.4, C3.+
  N1: U2.RD-, Bauteil5.D2
  N2: U3.B1, U9.CHAN1
  5V: U3.H2, U4.H2, U5.H2, U6.H2, U7.H2, U8.H2, Bauteil5.5V, U9.VCC, JP4.6, R3.Pin_0
  N3: U4.B1, U9.CHAN0
  N4: U5.B1, U9.CHAN3
  N5: U6.B1, U9.CHAN5
  N6: U7.B1, U9.CHAN2
  N7: U8.B1, U9.CHAN4
  N8: Bauteil4.AUD, U9.CHAN14
  N9: LED1.red_anode, LED1.common_cathode
  N10: LED1.blue_anode, LED1.green_anode
  N11: Bauteil5.D3, U9.S3
  N12: Bauteil5.D4, U9.S2
  N13: Bauteil5.D5, U9.S1
  N14: Bauteil5.D6, U9.S0
  N15: Bauteil5.A7, U9.COM
  N16: Bauteil5.A3, JP4.3
  N17: U9.CHAN15, Bauteil6.S
  N18: U9.CHAN8, JP4.5
  N19: JP4.1, R3.Pin_1, C3.-

notes:
  Pin 1...6
