# Fritzing sketch Tiny_HP-C4280_Enabler (saved by Fritzing 0.8.5b)
breadboards: 2

parts:
  Bauteil3 = Arduino Uno (Rev3)
  U11 = RELAY-SOLIDSTATE [package=relay-s108t02]
  U12 = RELAY-SOLIDSTATE [package=relay-s108t02]
  U13 = RELAY-SOLIDSTATE [package=relay-s108t02]
  U14 = RELAY-SOLIDSTATE [package=relay-s108t02]
  R1 = Resistor [tolerance=±5% resistance=1k package=THT]
  JP1 = Header 6 [package=molex-1x6-ra_lock]
  U15 = attiny85 [package=dip]
  U16 = attiny85 [package=dip]
  C3 = Capacitor Polarized [package=cpol-radial-10uf-25v]
  X1 = USB Connectors [package=usb-a-s-silk-female]
  J1 = AVR ISP 6 Pin [package=2x3-ns]
  JP5 = Header 6 [package=molex-1x6-ra_lock]
  JP6 = Header 6 [package=molex-1x6-ra_lock]

nets:
  N1: Bauteil3.D10_PWM/SS, U15.Pin_1, U16.Pin_4, J1.5, JP5.3, JP6.3
  N2: Bauteil3.D11_PWM/MOSI, U15.Pin_4, J1.4, JP5.4, JP6.4
  N3: Bauteil3.D12/MISO, U15.Pin_5, J1.1, JP5.5, JP6.5
  N4: Bauteil3.D13/SCK, U15.Pin_6, J1.3, JP5.6, JP6.6
  GND: Bauteil3.GND, R1.Pin_1, U16.Pin_8, C3.+, X1.GND, J1.6, JP5.1, JP6.1
  N5: Bauteil3.RESET, C3.-
  N6: Bauteil3.5V, U16.Pin_1, X1.VBUS, J1.2, JP5.2, JP6.2
  N7: U11.T1, U12.T1, U13.T1, JP1.3
  N8: U11.T2, JP1.6
  N9: U11.+, U15.Pin_3
  N10: U11.-, U12.-, U13.-, U14.-, R1.Pin_0
  N11: U12.T2, JP1.5
  N12: U12.+, U15.Pin_2
  N13: U13.T2, JP1.4
  N14: U13.+, U16.Pin_3
  N15: U14.T1, JP1.1
  N16: U14.T2, JP1.2, U16.Pin_6
  N17: U14.+, U16.Pin_2
  N18: U15.Pin_8, U16.Pin_5

notes:
  ?? 0.22uF
  (should be 10uF...)
  (needed at all?!)
  2:VCC - 4:MOSI - 6:GND
  1:MISO - 3:SCK - 5:RST
  same as ICSP except for RST to 10
  HP-C4280_Enabler in ATtiny84
  Arduino Uno as ATtiny84 ISP
