# Fritzing sketch Uno_ChargePump_AnalogOut (saved by Fritzing 0.8.5b)
breadboards: 1

parts:
  IC1 = Dual Op-Amp [package=dip08]
  D1 = Diode [package=diode-1n4148]
  R1 = Resistor [tolerance=±5% resistance=6.8k package=THT]
  C1 = Electrolytic Capacitor [capacitance=0.22µF voltage=20V package="100 mil [THT, electrolytic]"]
  Bauteil1 = Arduino Uno (Rev3)
  D2 = Diode [package=diode-1n4148]
  D3 = Diode [package=diode-1n4148]
  D4 = Diode [package=diode-1n4148]
  C2 = Electrolytic Capacitor [capacitance=0.22µF voltage=20V package="100 mil [THT, electrolytic]"]
  C3 = Electrolytic Capacitor [capacitance=0.22µF voltage=20V package="100 mil [THT, electrolytic]"]
  C4 = Electrolytic Capacitor [capacitance=0.22µF voltage=20V package="100 mil [THT, electrolytic]"]
  R2 = Resistor [tolerance=±5% resistance=6.8k package=THT]
  R3 = Resistor [tolerance=±5% resistance=3.3k package=THT]
  C5 = Electrolytic Capacitor [capacitance=470µF package="100 mil [THT, electrolytic]"]
  R4 = Resistor [tolerance=±5% resistance=150 package=THT]
  U1 = RELAY-SOLIDSTATE [package=relay-s108t02]
  U2 = RELAY-SOLIDSTATE [package=relay-s108t02]
  R5 = Resistor [tolerance=±5% resistance=1k package=THT]
  R6 = Resistor [tolerance=±5% resistance=1k package=THT]

nets:
  N1: IC1.A_OUT, IC1.A_-IN, U1.T1
  N2: IC1.A_+IN, C5.+, R4.Pin_1
  GND: IC1.A_V-, Bauteil1.GND, C4.-, R3.Pin_1, C5.-, R5.Pin_1, R6.Pin_0
  N3: IC1.B_+IN, D1.C, R1.Pin_0, C4.+
  N4: IC1.B_-IN, IC1.B_OUT, U2.T1
  N5: D1.A, C1.+, D2.C
  N6: R1.Pin_1, R2.Pin_0
  N7: C1.-, Bauteil1.D2, C3.-
  N8: Bauteil1.A0, R2.Pin_1, R3.Pin_0
  N9: Bauteil1.D9_PWM, U2.+
  N10: Bauteil1.D10_PWM/SS, U1.+
  N11: Bauteil1.D11_PWM/MOSI, R4.Pin_0
  N12: Bauteil1.D3_PWM, C2.-
  N13: Bauteil1.D4, D4.A
  N14: D2.A, D3.C, C2.+
  N15: D3.A, D4.C, C3.+
  N16: U1.-, R5.Pin_0
  N17: U2.-, R6.Pin_1

notes:
  0.22uF is bad
  need 2uF
  TCA0372
  MOS RELAY
  DAC: 3...15V
  DAC: 0...5V
  Current Amp.
  PWM Relay
