# Fritzing sketch Uno_EditFC28_USB (saved by Fritzing 0.8.5b)
circuit board: 8.46667cm x 5.64444cm
breadboards: 1

parts:
  Part1 = Arduino Uno (Rev3)
  JP1 = Header 6 [package=molex-1x6_lock]
  JP2 = Header 3 [package=molex-1x3_lock]
  JP3 = Header 2 [package=molex-1x2_lock]

nets:
  N1: Part1.D0/RX, JP1.3, JP2.2
  N2: Part1.D1/TX, JP1.2, JP2.1
  N3: Part1.RESET, Part1.GND, JP2.3
  N4: JP1.4, JP3.2
  N5: JP1.5, JP3.1
