# Fritzing sketch Uno_OWMaster (saved by Fritzing 0.8.5b)

parts:
  Bauteil1 = Arduino Uno (Rev3)
  BAT2 = Battery Holders [package=battcon_245mm]
  U1 = MAGJACK-POE [package=magjack-poe]
  R1 = Resistor [tolerance=±5% resistance=4.7k package=THT]

nets:
  1wire bus / MicroLAN: Bauteil1.D13/SCK, BAT2.+, U1.RD-, R1.Pin_1
  GND: Bauteil1.GND, BAT2.-, U1.SHIELD
  N1: Bauteil1.5V, U1.TCT, R1.Pin_0

notes:
  Parasitary Power Pull-Up
  1wire bus / MicroLan
  iButton interface
