# Fritzing sketch Uno_OWMaster_OWSlave (saved by Fritzing 0.8.5b)

parts:
  Bauteil1 = Arduino Uno (Rev3)
  Bauteil2 = Arduino Leonardo (Rev3b)
  R2 = Resistor [tolerance=±5% resistance=4.7k package=THT]

nets:
  N1: Bauteil1.D2, Bauteil2.D12/A11, R2.Pin_1
  GND: Bauteil1.GND, Bauteil2.GND
  N2: Bauteil2.5V, R2.Pin_0

notes:
  Yun: OWMaster
  (Leonardo compatible)
  Parasitary Power Pull-Up
  (Pin13 used also but
  disables uploading sketches)
  1wire bus / MicroLan
  Uno: OWSlave
  Pin2 since interrupt needed
