# Fritzing sketch Uno_OWSniffer (saved by Fritzing 0.8.5b)
circuit board: 8.46667cm x 5.64444cm

parts:
  Bauteil1 = Arduino Uno (Rev3)
  U1 = MAGJACK-POE [package=magjack-poe]

nets:
  GND: Bauteil1.GND, Bauteil1.RESET, U1.SHIELD, U1.YLED-, U1.GLED-
  1wire bus / MicroLAN: Bauteil1.D1/TX, U1.RD-

notes:
  Use ATmega8U2 as UART only. Thus set
  RESET jumper to dis-
  able ATmega328P.
  Acts as SERIAL2USB
  ("RS-232") converter.
  1wire bus / MicroLan
  RESET jumper to dis-
  able ATmega328P
  Use ATmega8U2 as UART only.
  http://www.maximintegrated.com/en/app-notes/index.mvp/id/214
  http://blog.oscarliang.net/use-arduino-as-usb-serial-adapter-converter/
  RJ45 Pin: 4+5
