# Fritzing sketch Uno_OWSniffer (saved by Fritzing 0.8.5b)
circuit board: 8.46667cm x 5.64444cm

parts:
  Bauteil1 = Arduino Uno (Rev3)
  U1 = RJ45 Jack [package=rj45-8]
  J1 = M10X2 [package=2x10_lock]
  R1 = Resistor [tolerance=±5% resistance=4.7k package=THT]
  JP1 = Header 2 [package=screwterminal-3.5mm-2_lock]
  J2 = female pin header, 2 pins [form="♀ (female)"]
  JP8 = FTDI_BASIC [package=ftdi_basic]

nets (from the pcb view):
  N1: Bauteil1.D8, J1.6
  N2: Bauteil1.GND, U1.5, J1.4, JP1.1
  N3: Bauteil1.D1/TX, J1.20
  N4: Bauteil1.D2, J1.18
  N5: Bauteil1.D3_PWM, J1.16
  N6: Bauteil1.D4, J1.14
  N7: Bauteil1.D5_PWM, J1.12
  N8: Bauteil1.D6_PWM, J1.10
  N9: Bauteil1.D7, J1.8
  N10: Bauteil1.RESET, J1.2
  N11: Bauteil1.5V, R1.Pin_1, J2.pin1
  N12: U1.1, JP8.6
  N13: U1.2, JP8.5
  N14: U1.3, JP8.4
  N15: U1.4, J1.3, J1.5, J1.7, J1.9, J1.11, J1.13, J1.15, J1.17, J1.19, JP1.2
  N16: U1.6, JP8.3
  N17: U1.7, JP8.2
  N18: U1.8, JP8.1
  N19: J1.1, R1.Pin_0, J2.pin2

notes:
  Use ATmega8U2 as UART only. Thus set
  RESET jumper to dis-
  able ATmega328P.
  Acts as SERIAL2USB
  ("RS-232") converter.
  1wire bus / MicroLan
  RESET jumper to dis-
  able ATmega328P
  Use ATmega8U2 as UART only.
  http://www.maximintegrated.com/en/app-notes/index.mvp/id/214
  http://blog.oscarliang.net/use-arduino-as-usb-serial-adapter-converter/
  RJ45 Pin: 4+5
  RESET & PULL-UP
  JUMPER
