# Fritzing sketch Uno_Programmer (saved by Fritzing 0.8.5b)
circuit board: 8.46667cm x 5.64444cm
breadboards: 1

parts:
  Bauteil3 = Arduino Uno (Rev3)
  C3 = Capacitor Polarized [package=cpol-radial-10uf-25v]
  J1 = AVR ISP 6 Pin [package=2x3-ns]
  JP5 = Header 6 [package=molex-1x6-ra_lock]
  JP6 = Header 6 [package=molex-1x6-ra_lock]
  U17 = ZIFSOCKET-28-3 [package=dil28-3-zif_socket]  # not connected

nets:
  N1: Bauteil3.D10_PWM/SS, J1.5, JP5.3, JP6.3
  N2: Bauteil3.D11_PWM/MOSI, J1.4, JP5.4, JP6.4
  N3: Bauteil3.D12/MISO, J1.1, JP5.5, JP6.5
  N4: Bauteil3.D13/SCK, J1.3, JP5.6, JP6.6
  GND: Bauteil3.GND, C3.+, J1.6, JP5.1, JP6.1
  N5: Bauteil3.RESET, C3.-
  N6: Bauteil3.5V, J1.2, JP5.2, JP6.2

notes:
  ?? 0.22uF
  (should be 10uF...)
  (needed at all?!)
  2:VCC - 4:MOSI - 6:GND
  1:MISO - 3:SCK - 5:RST
  same as ICSP except for RST to 10
  ZIF socket on breadboard
  5:RST - 3:SCK - 1:MISO
  6:GND - 4:MOSI - 2:VCC
