# Fritzing sketch Uno_ppmUSBjoy (saved by Fritzing 0.8.5b)
circuit board: 8.46667cm x 5.64444cm
breadboards: 1

parts:
  Part1 = Arduino Uno (Rev3)
  D1 = Zener Diode [part_number=1N4732A-3.6V breakdown_voltage=3.6V package="300 mil [THT]"]
  D2 = Zener Diode [part_number=1N4732A-3.6V breakdown_voltage=3.6V package="300 mil [THT]"]
  JP1 = Header 4 [package=molex-1x4_lock]
  R1 = Resistor [tolerance=±5% resistance=68 package=THT]
  R2 = Resistor [tolerance=±5% resistance=68 package=THT]
  R3 = Resistor [tolerance=±5% resistance=2.2k package=THT]
  JP2 = Header 4 [package=molex-1x4_lock]
  TRS1 = Audio Jack (TRS) 3.5mm [package="4Ucon 08780 [THT]"]
  X3 = USB Connectors [package=usb-a-h]

nets:
  N1: Part1.GND, D1.anode, D2.anode, JP1.3, TRS1.Sleeve
  N2: Part1.D2, D2.cathode, R2.Pin_1
  N3: Part1.D3_PWM, TRS1.Tip
  N4: Part1.D7, D1.cathode, R1.Pin_1, R3.Pin_0
  N5: Part1.VIN, JP1.4, R3.Pin_1
  N6: JP1.1, R1.Pin_0
  N7: JP1.2, R2.Pin_0
  N8: JP2.1, X3.D-
  N9: JP2.2, X3.D+
  N10: JP2.3, X3.GND
  N11: JP2.4, X3.VBUS
